# Fritzing sketch HC-06 (saved by Fritzing 0.8.7b)
breadboards: 1

parts:
  Part1 = Arduino Leonardo (Rev3b)
  Part2 = HC-06 Bluetooth

nets:
  N1: Part1.5V, Part2.pin_4
  N2: Part1.GND, Part2.pin_3
  N3: Part1.D10_PWM/A10, Part2.pin_2
  N4: Part1.D11_PWM, Part2.pin_1

custom parts:
  HC-06 Bluetooth: Bluetooth
