# Fritzing sketch HC-SR04 (saved by Fritzing 0.8.7b)
breadboards: 1

parts:
  Part1 = Arduino Leonardo (Rev3b)
  Part2 = SRF05 Ultrasonic Rangefinder

nets:
  N1: Part1.D7, Part2.Trig
  5V: Part1.5V, Part2.VCC
  N2: Part1.D8/A8, Part2.Echo
  GND: Part1.GND, Part2.GND
