# Fritzing sketch LED (saved by Fritzing 0.8.7b)

parts:
  Part1 = Arduino Leonardo (Rev3b)
  LED1 = LED - 5mm [color="Red (635nm)" package="5 mm [THT]"]

nets:
  N1: Part1.D13_PWM, LED1.anode
  N2: Part1.GND, LED1.cathode
