# Fritzing sketch MD1_3 Dual Motor Controller (saved by Fritzing 0.8.7b)

parts:
  Part1 = Arduino Leonardo (Rev3b)
  Part2 = YL-44 Buzzer
  M1 = DC Motor
  M2 = DC Motor
  BAT1 = BC9VPC [package=bc9vpc]

nets:
  N1: Part1.D2/SDA, Part2.pin_9
  N2: Part1.D3_PWM/SCL, Part2.pin_8
  N3: Part1.D4/A6, Part2.pin_11
  N4: Part1.D5_PWM, Part2.pin_10
  N5: Part1.GND, Part2.pin_6, BAT1.V+
  N6: Part2.pin_1, M1.pin_2
  N7: Part2.pin_2, M1.pin_1
  N8: Part2.pin_3, M2.pin_1
  N9: Part2.pin_4, M2.pin_2
  N10: Part2.pin_7, BAT1.V-

custom parts:
  YL-44 Buzzer: Buzzer
