# Fritzing sketch RoboBase (saved by Fritzing 0.8.7b)

parts:
  Part1 = Arduino Leonardo (Rev3b)
  HC-SR04_Ultrasonic_Sensor = SRF05 Ultrasonic Rangefinder  # not connected
  HC-06_Bluetooth = HC-06  # not connected
  LED1 = smd LED [color="Red (633nm)" package="0805 [SMD]"]
  Buzzer_YL-44 = Breakout Board for Electret Microphone  # not connected
  L298N_DC_Stepper_Motor_Driver_Controller_Board_Module_for_Arduino = DC Motor  # not connected

nets:
  N1: Part1.D13_PWM, LED1.anode
  N2: Part1.GND, LED1.cathode
