# Fritzing sketch YL-44 (saved by Fritzing 0.8.7b)
breadboards: 1

parts:
  Part1 = Arduino Leonardo (Rev3b)
  Part2 = YL-44 Buzzer

nets:
  N1: Part1.5V, Part2.pin_1
  N2: Part1.GND, Part2.pin_3
  N3: Part1.D9_PWM/A9, Part2.pin_2

custom parts:
  YL-44 Buzzer: Buzzer
